// Logisim project 02.Xi.circ as structural Verilog: 1 circuit, main circuit main
module main (
  input  a3,
  input  a2,
  input  a1,
  input  a0,
  input  b3,
  input  b2,
  input  b1,
  input  b0,
  input  CS2,
  input  CS1,
  input  CS0,
  output e,
  output d,
  output Z0,
  output x3,
  output x2,
  output x1,
  output x0
);

  wire n7400_1_p2, n7400_1_p5, n7408_1_p2, n7408_1_p3, n7408_1_p6, n7408_1_p9, n7408_2_p2, n7408_2_p3,
       n7408_2_p6, n7408_2_p9, n7486_1_p2, n7486_1_p3, n7486_1_p8, n7486_1_p9, n74138_1_p3, n74138_1_p4,
       n74138_1_p5, n74138_1_p7, n74138_1_p9, n74138_1_p11, n74138_1_p13, n74138_1_p15;

  // _74138 74138_1: pin names not known; wires that end beside it: 1'b0, 1'b0, n74138_1_p3, n74138_1_p4, n74138_1_p5, 1'b1, n74138_1_p7, 1'b0, n74138_1_p9, 1'b0, n74138_1_p11, CS2, n74138_1_p13, CS1, n74138_1_p15, CS0, 1'b1
  // _7400 7400_1: pin names not known; wires that end beside it: 1'b0, n7400_1_p2, n74138_1_p11, n74138_1_p3, n7400_1_p5, n74138_1_p4, n74138_1_p13, 1'b1
  // _7408 7408_1: pin names not known; wires that end beside it: 1'b0, n7408_1_p2, n7408_1_p3, n74138_1_p5, n7400_1_p2, n7408_1_p6, b3, n7408_1_p6, n7408_1_p9, n74138_1_p7, n7400_1_p2, n74138_1_p9, b2, 1'b1
  // _7402 7402_1: pin names not known; wires that end beside it: 1'b0, 1'b1
  // _7408 7408_2: pin names not known; wires that end beside it: 1'b0, n7408_2_p2, n7408_2_p3, n74138_1_p5, n7400_1_p2, n7408_2_p6, b1, n7408_2_p6, n7408_2_p9, n74138_1_p7, n7400_1_p2, n74138_1_p13, b0, 1'b1
  // _7404 7404_1: pin names not known; wires that end beside it: 1'b0, e, d, n7408_1_p2, n74138_1_p15, Z0, n7408_2_p2, 1'b1
  // _7486 7486_1: pin names not known; wires that end beside it: 1'b0, n7486_1_p2, n7486_1_p3, a2, n7400_1_p5, n7400_1_p5, a3, n7486_1_p8, n7486_1_p9, n7400_1_p5, a0, a1, n7400_1_p5, 1'b1
  // _7432 7432_1: pin names not known; wires that end beside it: 1'b0, x2, x3, n7486_1_p2, n7486_1_p3, n7408_1_p9, n7408_1_p3, x1, x0, n7486_1_p8, n7486_1_p9, n7408_2_p3, n7408_2_p9, 1'b1
endmodule
