// Logisim project 04.Complete_ALU_UnOptimized.circ as structural Verilog: 2 circuits, main circuit main
module main (
  input  CS2,
  input  CS1,
  input  CS0,
  input  a3,
  input  a2,
  input  a1,
  input  a0,
  input  b3,
  input  b2,
  input  b1,
  input  b0,
  output C,
  output S,
  output V,
  output Z,
  output s3,
  output s2,
  output s1,
  output s0
);

  wire n7400_1_p2, n7400_1_p5, n7402_1_p6, n7402_1_p7, n7402_1_p12, n7402_1_p13, n7404_1_p4, n7408_1_p2,
       n7408_1_p3, n7408_1_p6, n7408_1_p9, n7408_2_p2, n7408_2_p3, n7408_2_p6, n7408_2_p9, n7432_1_p2,
       n7432_1_p3, n7432_1_p6, n7432_1_p8, n7432_2_p3, n7432_2_p7, n7432_3_p2, n7432_3_p8, n7432_3_p9,
       n7486_1_p3, n7486_1_p7, n7486_1_p11, n7486_1_p12, n7486_1_p13, n7486_2_p2, n7486_2_p3, n7486_2_p8,
       n7486_2_p9, n74138_1_p2, n74138_1_p3, n74138_1_p4, n74138_1_p6, n74138_1_p8, n74138_1_p10,
       n74138_1_p12, n74138_1_p14;

  // _74138 74138_1: pin names not known; wires that end beside it: 1'b0, n74138_1_p2, n74138_1_p3, n74138_1_p4, 1'b1, n74138_1_p6, 1'b0, n74138_1_p8, 1'b0, n74138_1_p10, CS2, n74138_1_p12, CS1, n74138_1_p14, CS0, 1'b1
  _7483 u_7483_1 (
    ._1__A4(n7486_1_p13), ._2__S3(s2), ._3__A3(n7432_3_p2), ._4__B3(n7432_1_p3), ._5__Vcc(1'b1), ._6__S2(s1),
    ._7__B2(n7432_1_p2), ._8__A2(n7432_3_p8), ._16__B4(n7486_1_p11), ._15__S4(S), .Cout(C),
    ._13__Cin(n7404_1_p4), ._12__GND(1'b0), ._11__B1(n7432_1_p8), ._10__A1(n7432_3_p9), ._9__S1(s0));
  // _7400 7400_1: pin names not known; wires that end beside it: 1'b0, n7400_1_p2, n74138_1_p10, n74138_1_p2, n7400_1_p5, n74138_1_p3, n74138_1_p12, 1'b1
  // _7408 7408_1: pin names not known; wires that end beside it: 1'b0, n7408_1_p2, n7408_1_p3, n74138_1_p4, n7400_1_p2, n7408_1_p6, b3, n7408_1_p6, n7408_1_p9, n74138_1_p6, n7400_1_p2, n74138_1_p8, b2, 1'b1
  // _7486 7486_1: pin names not known; wires that end beside it: 1'b0, V, n7486_1_p3, n7486_1_p3, S, C, n7486_1_p7, Z, n7486_1_p7, 1'b1, n7486_1_p11, n7486_1_p12, n7486_1_p13, 1'b1
  // _7402 7402_1: pin names not known; wires that end beside it: 1'b0, b1, n7408_1_p2, n7408_1_p2, b3, n7402_1_p6, n7402_1_p7, n7408_1_p2, n7408_1_p2, b0, b2, n7402_1_p12, n7402_1_p13, 1'b1
  // _7408 7408_2: pin names not known; wires that end beside it: 1'b0, n7408_2_p2, n7408_2_p3, n74138_1_p4, n7400_1_p2, n7408_2_p6, b1, n7408_2_p6, n7408_2_p9, n74138_1_p6, n7400_1_p2, n74138_1_p12, b0, 1'b1
  // _7432 7432_1: pin names not known; wires that end beside it: 1'b0, n7432_1_p2, n7432_1_p3, n7402_1_p6, n7402_1_p13, n7432_1_p6, n7432_1_p6, n7432_1_p8, n7486_1_p11, n7432_1_p6, n7402_1_p7, n7402_1_p12, n7432_1_p6, 1'b1
  // _7404 7404_1: pin names not known; wires that end beside it: 1'b0, n7432_1_p6, n74138_1_p14, n7404_1_p4, n7408_2_p2, 1'b1
  // _7486 7486_2: pin names not known; wires that end beside it: 1'b0, n7486_2_p2, n7486_2_p3, a2, n7400_1_p5, n7400_1_p5, a3, n7486_2_p8, n7486_2_p9, n7400_1_p5, a0, a1, n7400_1_p5, 1'b1
  // _7432 7432_2: pin names not known; wires that end beside it: 1'b0, n7486_1_p12, n7432_2_p3, n7432_2_p3, s2, S, n7432_2_p7, n7432_2_p7, s1, s0, 1'b1, 1'b1
  // _7432 7432_3: pin names not known; wires that end beside it: 1'b0, n7432_3_p2, n7486_1_p13, n7486_2_p2, n7486_2_p3, n7408_1_p9, n7408_1_p3, n7432_3_p8, n7432_3_p9, n7486_2_p8, n7486_2_p9, n7408_2_p3, n7408_2_p9, 1'b1

  assign s3 = S;
endmodule

module _7483 (
  input  _1__A4,
  input  _16__B4,
  input  _3__A3,
  input  _4__B3,
  input  _13__Cin,
  input  _5__Vcc,
  input  _12__GND,
  input  _11__B1,
  input  _7__B2,
  input  _10__A1,
  input  _8__A2,
  output _2__S3,
  output _15__S4,
  output Cout,
  output _6__S2,
  output _9__S1
);

  wire and_1_out, and_2_out, and_3_out, and_4_out, and_5_out, and_6_out, and_7_out, and_8_out, and_9_out,
       and_10_out, and_11_out, and_12_out, and_13_out, and_14_out, nand_1_out, nand_2_out, nand_3_out,
       nand_4_out, nor_1_out, nor_2_out, nor_3_out, nor_4_out, nor_6_out, nor_7_out, nor_8_out, not_1_out,
       not_2_out, not_3_out, not_4_out, not_5_out, not_6_out;

  nand nand_1 (nand_1_out, _16__B4, _1__A4);
  nor nor_1 (nor_1_out, _16__B4, _1__A4);
  nand nand_2 (nand_2_out, _4__B3, _3__A3);
  nor nor_2 (nor_2_out, _4__B3, _3__A3);
  nand nand_3 (nand_3_out, _7__B2, _8__A2);
  nor nor_3 (nor_3_out, _7__B2, _8__A2);
  nand nand_4 (nand_4_out, _11__B1, _10__A1);
  nor nor_4 (nor_4_out, _11__B1, _10__A1);
  and and_1 (and_1_out, nor_2_out, nand_1_out);
  and and_2 (and_2_out, nor_3_out, nand_1_out, nand_2_out);
  and and_3 (and_3_out, nor_4_out, nand_1_out, nand_2_out, nand_3_out);
  and and_4 (and_4_out, nand_1_out, nand_2_out, nand_3_out, nand_4_out, not_2_out);
  not not_1 (not_1_out, nor_1_out);
  and and_5 (and_5_out, nor_3_out, nand_2_out);
  and and_6 (and_6_out, nor_4_out, nand_2_out, nand_3_out);
  and and_7 (and_7_out, nand_2_out, nand_3_out, nand_4_out, not_2_out);
  not not_2 (not_2_out, _13__Cin);
  not not_3 (not_3_out, nor_2_out);
  and and_8 (and_8_out, nor_4_out, nand_3_out);
  and and_9 (and_9_out, nand_3_out, nand_4_out, not_2_out);
  not not_4 (not_4_out, nor_3_out);
  and and_10 (and_10_out, nand_4_out, not_2_out);
  not not_5 (not_5_out, nor_4_out);
  not not_6 (not_6_out, not_2_out);
  nor nor_5 (Cout, nor_1_out, and_1_out, and_2_out, and_3_out, and_4_out);
  and and_11 (and_11_out, nand_1_out, not_1_out);
  and and_12 (and_12_out, nand_2_out, not_3_out);
  and and_13 (and_13_out, nand_3_out, not_4_out);
  and and_14 (and_14_out, nand_4_out, not_5_out);
  xor xor_1 (_15__S4, and_11_out, nor_6_out);
  nor nor_6 (nor_6_out, nor_2_out, and_5_out, and_6_out, and_7_out);
  xor xor_2 (_2__S3, and_12_out, nor_7_out);
  nor nor_7 (nor_7_out, nor_3_out, and_8_out, and_9_out);
  xor xor_3 (_6__S2, and_13_out, nor_8_out);
  nor nor_8 (nor_8_out, nor_4_out, and_10_out);
  xor xor_4 (_9__S1, and_14_out, not_6_out);
endmodule
