// Logisim project ALU_32_bit.circ as structural Verilog: 1 circuit, main circuit ALU_32_bit
module ALU_32_bit (
  input  [5:0] OpCode,
  input  Invert_B_Signal,
  input  Cin,
  input  [31:0] A,
  input  [31:0] B,
  output Cout,
  output [31:0] C,
  output OVF
);

  wire one_bit_alu_1_c_out, one_bit_alu_2_c_out, one_bit_alu_3_c_out, one_bit_alu_4_c_out,
       one_bit_alu_5_c_out, one_bit_alu_6_c_out, one_bit_alu_7_c_out, one_bit_alu_8_c_out,
       one_bit_alu_9_c_out, one_bit_alu_10_c_out, one_bit_alu_11_c_out, one_bit_alu_12_c_out,
       one_bit_alu_13_c_out, one_bit_alu_14_c_out, one_bit_alu_15_c_out, one_bit_alu_16_c_out,
       one_bit_alu_17_c_out, one_bit_alu_18_c_out, one_bit_alu_19_c_out, one_bit_alu_20_c_out,
       one_bit_alu_21_c_out, one_bit_alu_22_c_out, one_bit_alu_23_c_out, one_bit_alu_24_c_out,
       one_bit_alu_25_c_out, one_bit_alu_26_c_out, one_bit_alu_27_c_out, one_bit_alu_28_c_out,
       one_bit_alu_29_c_out, one_bit_alu_30_c_out, one_bit_alu_31_c_out, one_bit_alu_final_1_set;

  one_bit_ALU one_bit_alu_1 (
    .ALU_OpCode(OpCode), .C_Out(one_bit_alu_1_c_out), .A(A[0]), .B(B[0]), .Invert_B_Signal(Cin),
    .ALU_Result_1(C[0]), .less(one_bit_alu_final_1_set), .C_In(Cin));
  one_bit_ALU one_bit_alu_2 (
    .ALU_OpCode(OpCode), .C_Out(one_bit_alu_2_c_out), .A(A[1]), .B(B[1]), .Invert_B_Signal(Invert_B_Signal),
    .ALU_Result_1(C[1]), .less(1'b0), .C_In(one_bit_alu_1_c_out));
  one_bit_ALU one_bit_alu_3 (
    .ALU_OpCode(OpCode), .C_Out(one_bit_alu_3_c_out), .A(A[2]), .B(B[2]), .Invert_B_Signal(Invert_B_Signal),
    .ALU_Result_1(C[2]), .less(1'b0), .C_In(one_bit_alu_2_c_out));
  one_bit_ALU one_bit_alu_4 (
    .ALU_OpCode(OpCode), .C_Out(one_bit_alu_4_c_out), .A(A[3]), .B(B[3]), .Invert_B_Signal(Invert_B_Signal),
    .ALU_Result_1(C[3]), .less(1'b0), .C_In(one_bit_alu_3_c_out));
  one_bit_ALU one_bit_alu_5 (
    .ALU_OpCode(OpCode), .C_Out(one_bit_alu_5_c_out), .A(A[4]), .B(B[4]), .Invert_B_Signal(Invert_B_Signal),
    .ALU_Result_1(C[4]), .less(1'b0), .C_In(one_bit_alu_4_c_out));
  one_bit_ALU one_bit_alu_6 (
    .ALU_OpCode(OpCode), .C_Out(one_bit_alu_6_c_out), .A(A[5]), .B(B[5]), .Invert_B_Signal(Invert_B_Signal),
    .ALU_Result_1(C[5]), .less(1'b0), .C_In(one_bit_alu_5_c_out));
  one_bit_ALU one_bit_alu_7 (
    .ALU_OpCode(OpCode), .C_Out(one_bit_alu_7_c_out), .A(A[6]), .B(B[6]), .Invert_B_Signal(Invert_B_Signal),
    .ALU_Result_1(C[6]), .less(1'b0), .C_In(one_bit_alu_6_c_out));
  one_bit_ALU one_bit_alu_8 (
    .ALU_OpCode(OpCode), .C_Out(one_bit_alu_8_c_out), .A(A[7]), .B(B[7]), .Invert_B_Signal(Invert_B_Signal),
    .ALU_Result_1(C[7]), .less(1'b0), .C_In(one_bit_alu_7_c_out));
  one_bit_ALU one_bit_alu_9 (
    .ALU_OpCode(OpCode), .C_Out(one_bit_alu_9_c_out), .A(A[9]), .B(B[9]), .Invert_B_Signal(Invert_B_Signal),
    .ALU_Result_1(C[9]), .less(1'b0), .C_In(one_bit_alu_10_c_out));
  one_bit_ALU one_bit_alu_10 (
    .ALU_OpCode(OpCode), .C_Out(one_bit_alu_10_c_out), .A(A[8]), .B(B[8]), .Invert_B_Signal(Invert_B_Signal),
    .ALU_Result_1(C[8]), .less(1'b0), .C_In(one_bit_alu_8_c_out));
  one_bit_ALU one_bit_alu_11 (
    .ALU_OpCode(OpCode), .C_Out(one_bit_alu_11_c_out), .A(A[10]), .B(B[10]),
    .Invert_B_Signal(Invert_B_Signal), .ALU_Result_1(C[10]), .less(1'b0), .C_In(one_bit_alu_9_c_out));
  one_bit_ALU one_bit_alu_12 (
    .ALU_OpCode(OpCode), .C_Out(one_bit_alu_12_c_out), .A(A[11]), .B(B[11]),
    .Invert_B_Signal(Invert_B_Signal), .ALU_Result_1(C[11]), .less(1'b0), .C_In(one_bit_alu_11_c_out));
  one_bit_ALU one_bit_alu_13 (
    .ALU_OpCode(OpCode), .C_Out(one_bit_alu_13_c_out), .A(A[12]), .B(B[12]),
    .Invert_B_Signal(Invert_B_Signal), .ALU_Result_1(C[12]), .less(1'b0), .C_In(one_bit_alu_12_c_out));
  one_bit_ALU one_bit_alu_14 (
    .ALU_OpCode(OpCode), .C_Out(one_bit_alu_14_c_out), .A(A[13]), .B(B[13]),
    .Invert_B_Signal(Invert_B_Signal), .ALU_Result_1(C[13]), .less(1'b0), .C_In(one_bit_alu_13_c_out));
  one_bit_ALU one_bit_alu_15 (
    .ALU_OpCode(OpCode), .C_Out(one_bit_alu_15_c_out), .A(A[14]), .B(B[14]),
    .Invert_B_Signal(Invert_B_Signal), .ALU_Result_1(C[14]), .less(1'b0), .C_In(one_bit_alu_14_c_out));
  one_bit_ALU one_bit_alu_16 (
    .ALU_OpCode(OpCode), .C_Out(one_bit_alu_16_c_out), .A(A[15]), .B(B[15]),
    .Invert_B_Signal(Invert_B_Signal), .ALU_Result_1(C[15]), .less(1'b0), .C_In(one_bit_alu_15_c_out));
  one_bit_ALU one_bit_alu_17 (
    .ALU_OpCode(OpCode), .C_Out(one_bit_alu_17_c_out), .A(A[16]), .B(B[16]),
    .Invert_B_Signal(Invert_B_Signal), .ALU_Result_1(C[16]), .less(1'b0), .C_In(one_bit_alu_16_c_out));
  one_bit_ALU one_bit_alu_18 (
    .ALU_OpCode(OpCode), .C_Out(one_bit_alu_18_c_out), .A(A[17]), .B(B[17]),
    .Invert_B_Signal(Invert_B_Signal), .ALU_Result_1(C[17]), .less(1'b0), .C_In(one_bit_alu_17_c_out));
  one_bit_ALU one_bit_alu_19 (
    .ALU_OpCode(OpCode), .C_Out(one_bit_alu_19_c_out), .A(A[18]), .B(B[18]),
    .Invert_B_Signal(Invert_B_Signal), .ALU_Result_1(C[18]), .less(1'b0), .C_In(one_bit_alu_18_c_out));
  one_bit_ALU one_bit_alu_20 (
    .ALU_OpCode(OpCode), .C_Out(one_bit_alu_20_c_out), .A(A[19]), .B(B[19]),
    .Invert_B_Signal(Invert_B_Signal), .ALU_Result_1(C[19]), .less(1'b0), .C_In(one_bit_alu_19_c_out));
  one_bit_ALU one_bit_alu_21 (
    .ALU_OpCode(OpCode), .C_Out(one_bit_alu_21_c_out), .A(A[20]), .B(B[20]),
    .Invert_B_Signal(Invert_B_Signal), .ALU_Result_1(C[20]), .less(1'b0), .C_In(one_bit_alu_20_c_out));
  one_bit_ALU one_bit_alu_22 (
    .ALU_OpCode(OpCode), .C_Out(one_bit_alu_22_c_out), .A(A[21]), .B(B[21]),
    .Invert_B_Signal(Invert_B_Signal), .ALU_Result_1(C[21]), .less(1'b0), .C_In(one_bit_alu_21_c_out));
  one_bit_ALU one_bit_alu_23 (
    .ALU_OpCode(OpCode), .C_Out(one_bit_alu_23_c_out), .A(A[22]), .B(B[22]),
    .Invert_B_Signal(Invert_B_Signal), .ALU_Result_1(C[22]), .less(1'b0), .C_In(one_bit_alu_22_c_out));
  one_bit_ALU one_bit_alu_24 (
    .ALU_OpCode(OpCode), .C_Out(one_bit_alu_24_c_out), .A(A[23]), .B(B[23]),
    .Invert_B_Signal(Invert_B_Signal), .ALU_Result_1(C[23]), .less(1'b0), .C_In(one_bit_alu_23_c_out));
  one_bit_ALU one_bit_alu_25 (
    .ALU_OpCode(OpCode), .C_Out(one_bit_alu_25_c_out), .A(A[24]), .B(B[24]),
    .Invert_B_Signal(Invert_B_Signal), .ALU_Result_1(C[24]), .less(1'b0), .C_In(one_bit_alu_24_c_out));
  one_bit_ALU one_bit_alu_26 (
    .ALU_OpCode(OpCode), .C_Out(one_bit_alu_26_c_out), .A(A[25]), .B(B[25]),
    .Invert_B_Signal(Invert_B_Signal), .ALU_Result_1(C[25]), .less(1'b0), .C_In(one_bit_alu_25_c_out));
  one_bit_ALU one_bit_alu_27 (
    .ALU_OpCode(OpCode), .C_Out(one_bit_alu_27_c_out), .A(A[26]), .B(B[26]),
    .Invert_B_Signal(Invert_B_Signal), .ALU_Result_1(C[26]), .less(1'b0), .C_In(one_bit_alu_26_c_out));
  one_bit_ALU one_bit_alu_28 (
    .ALU_OpCode(OpCode), .C_Out(one_bit_alu_28_c_out), .A(A[27]), .B(B[27]),
    .Invert_B_Signal(Invert_B_Signal), .ALU_Result_1(C[27]), .less(1'b0), .C_In(one_bit_alu_27_c_out));
  one_bit_ALU one_bit_alu_29 (
    .ALU_OpCode(OpCode), .C_Out(one_bit_alu_29_c_out), .A(A[28]), .B(B[28]),
    .Invert_B_Signal(Invert_B_Signal), .ALU_Result_1(C[28]), .less(1'b0), .C_In(one_bit_alu_28_c_out));
  one_bit_ALU one_bit_alu_30 (
    .ALU_OpCode(OpCode), .C_Out(one_bit_alu_30_c_out), .A(A[29]), .B(B[29]),
    .Invert_B_Signal(Invert_B_Signal), .ALU_Result_1(C[29]), .less(1'b0), .C_In(one_bit_alu_29_c_out));
  one_bit_ALU one_bit_alu_31 (
    .ALU_OpCode(OpCode), .C_Out(one_bit_alu_31_c_out), .A(A[30]), .B(B[30]),
    .Invert_B_Signal(Invert_B_Signal), .ALU_Result_1(C[30]), .less(1'b0), .C_In(one_bit_alu_30_c_out));
  one_bit_ALU_Final one_bit_alu_final_1 (
    .ALU_OpCode(OpCode), .C_Out(Cout), .A(A[31]), .B(B[31]), .Invert_B_Signal(Invert_B_Signal),
    .ALU_Result_1(C[31]), .less(1'b0), .C_In(one_bit_alu_31_c_out), .OVF(OVF), .Set(one_bit_alu_final_1_set));
endmodule
