// Logisim project FPA (group_3).circ as structural Verilog: 9 circuits, main circuit main
module main (
  input  [31:0] A,
  input  [31:0] B,
  output U,
  output O,
  output [31:0] OUtput
);

  Floating_point_adder FPA (.X(A), .Y(B), .Out(OUtput), .OVERFLOW(O), .UNDERFLOW(U));

  // Notes on the sheet:
  //   Floating Point Adder
endmodule

module comparator (
  input  [10:0] X,
  input  [10:0] Y,
  output X_Y,
  output [10:0] LARGER,
  output [4:0] DIFFERENCE
);

  wire ALU_2_n;
  wire [10:0] MUX_2_out, negator_1_out;
  wire [10:5] MUX_3_out;
  wire [15:0] ALU_alu_out;

  ALU_16_bit ALU (
    .ALU_A_IN({{5{1'b0}}, X}), .ALU_B_IN({{5{1'b0}}, Y}), .OP_CODE(3'b001), .ALU_OUT(ALU_alu_out), .N(X_Y));  // open: Z
  MUX_11_bit MUX (.in_1(X), ._1(Y), .SELECT(X_Y), .OUT(LARGER));
  Negator #(.width(11)) negator_1 (.in(ALU_alu_out[10:0]), .out(negator_1_out));
  MUX_11_bit MUX_2 (.in_1(ALU_alu_out[10:0]), ._1(negator_1_out), .SELECT(X_Y), .OUT(MUX_2_out));
  ALU_16_bit ALU_2 (
    .ALU_A_IN({{5{1'b0}}, MUX_2_out}), .ALU_B_IN(16'h1f), .OP_CODE(3'b001), .N(ALU_2_n));  // open: ALU_OUT, Z
  MUX_11_bit MUX_3 (.in_1(11'h1f), ._1(MUX_2_out), .SELECT(ALU_2_n), .OUT({MUX_3_out, DIFFERENCE}));

  // Notes on the sheet:
  //   finds diff
  //   finds larger
  //   makes diff pos if neg
  //   max shamt can be 11111
endmodule

module Fraction_Sign (
  input  Sign,
  input  [31:0] Fraction,
  input  [10:0] Exponent,
  output [31:0] \output 
);

  wire bitfinder_1_found;
  wire [31:0] mux_32_bit_1_out_4, negator_1_out;

  BitFinder #(.width(11)) bitfinder_1 (.in(Exponent), .found(bitfinder_1_found));  // open: index
  Negator #(.width(32)) negator_1 (.in(Fraction), .out(negator_1_out));
  MUX_32_bit mux_32_bit_1 (._0(Fraction), ._1(negator_1_out), .S(Sign), .out_4(mux_32_bit_1_out_4));
  MUX_32_bit mux_32_bit_2 (._0({32{1'b0}}), ._1(mux_32_bit_1_out_4), .S(bitfinder_1_found), .out_4(\output ));
endmodule

module ALU_16_bit (
  input  [15:0] ALU_A_IN,
  input  [15:0] ALU_B_IN,
  input  [2:0] OP_CODE,
  output [15:0] ALU_OUT,
  output Z,
  output N
);

  wire adder_1_cout;
  wire [15:0] adder_1_out, and_1_out, multiplexer_1_out, multiplexer_2_out, multiplexer_3_out,
       multiplexer_4_out, not_1_out, or_1_out, shifter_1_out, shifter_2_out, subtractor_1_out, xor_1_out;

  Adder #(.width(16)) adder_1 (.a(ALU_A_IN), .b(ALU_B_IN), .out(adder_1_out), .cout(adder_1_cout));  // open: cin
  Subtractor #(.width(16)) subtractor_1 (
    .a(ALU_A_IN), .b(ALU_B_IN), .out(subtractor_1_out), .bin(adder_1_cout));  // open: bout
  assign and_1_out = ALU_A_IN & ALU_B_IN;  // AND_Gate and_1, 16 bits wide
  assign or_1_out = ALU_A_IN | ALU_B_IN;  // OR_Gate or_1, 16 bits wide
  assign not_1_out = ~ALU_A_IN;  // NOT_Gate not_1, 16 bits wide
  assign xor_1_out = ALU_A_IN ^ ALU_B_IN;  // XOR_Gate xor_1, 16 bits wide
  Shifter #(.width(16), .shift("rl")) shifter_1 (.in(ALU_A_IN), .\dist (4'b0001), .out(shifter_1_out));
  Shifter #(.width(16), .shift("rr")) shifter_2 (.in(ALU_A_IN), .\dist (4'b0001), .out(shifter_2_out));
  Multiplexer #(.width(16), .enable("false")) multiplexer_1 (
    .in0(adder_1_out), .in1(subtractor_1_out), .out(multiplexer_1_out), .sel(OP_CODE[0]));
  Multiplexer #(.width(16), .enable("false")) multiplexer_2 (
    .in0(and_1_out), .in1(or_1_out), .out(multiplexer_2_out), .sel(OP_CODE[0]));
  Multiplexer #(.width(16), .enable("false")) multiplexer_3 (
    .in0(not_1_out), .in1(xor_1_out), .out(multiplexer_3_out), .sel(OP_CODE[0]));
  Multiplexer #(.width(16), .enable("false")) multiplexer_4 (
    .in0(shifter_1_out), .in1(shifter_2_out), .out(multiplexer_4_out), .sel(OP_CODE[0]));
  nor nor_1 (Z, ALU_OUT[0], ALU_OUT[1], ALU_OUT[2], ALU_OUT[3], ALU_OUT[4], ALU_OUT[5], ALU_OUT[6], ALU_OUT[7], ALU_OUT[8], ALU_OUT[9], ALU_OUT[10], ALU_OUT[11], ALU_OUT[12], ALU_OUT[13], ALU_OUT[14], ALU_OUT[15]);
  Multiplexer #(.select(2), .width(16), .enable("false")) multiplexer_5 (
    .in0(multiplexer_1_out), .in1(multiplexer_2_out), .in2(multiplexer_3_out), .in3(multiplexer_4_out),
    .out(ALU_OUT), .sel(OP_CODE[2:1]));

  assign N = ALU_OUT[15];
endmodule

module MUX_11_bit (
  input  [10:0] in_1,
  input  [10:0] _1,
  input  SELECT,
  output [10:0] OUT
);

  // _74157 74157_1: pin names not known; wires that end beside it: SELECT, in_1[0], _1[0], OUT[0], in_1[1], _1[1], OUT[1], 1'b0, in_1[2], _1[2], OUT[2], in_1[3], _1[3], OUT[3]
  // _74157 74157_2: pin names not known; wires that end beside it: SELECT, in_1[4], _1[4], OUT[4], in_1[5], _1[5], OUT[5], 1'b0, in_1[7], _1[7], OUT[7], in_1[6], _1[6], OUT[6]
  // _74157 74157_3: pin names not known; wires that end beside it: SELECT, in_1[8], _1[8], OUT[8], in_1[9], _1[9], OUT[9], 1'b0, in_1[10], _1[10], OUT[10]
endmodule

module Normalizer (
  input  [31:0] Fraction,
  input  [10:0] Exponent,
  output [31:0] NORMALIZED_FRACTION,
  output [10:0] NORMALIZED_EXPONENT,
  output OVERFLOW,
  output UNDERFLOW
);

  wire alu_16_bit_1_n, alu_16_bit_1_z, bitfinder_1_found, n7408_1_p3;
  wire [0:0] COMP_with_28_x_y;
  wire [4:0] bitfinder_1_index, COMP_with_28_difference;
  wire [10:0] mux_11_bit_1_out;
  wire [15:0] alu_16_bit_1_alu_out;
  wire [31:0] shifter_1_out, shifter_2_out;

  BitFinder #(.width(32), .\type ("high1")) bitfinder_1 (
    .in(Fraction), .index(bitfinder_1_index), .found(bitfinder_1_found));
  MUX_11_bit mux_11_bit_1 (.in_1({11{1'b0}}), ._1(11'h1c), .SELECT(bitfinder_1_found), .OUT(mux_11_bit_1_out));
  comparator COMP_with_28 (
    .X({{6{1'b0}}, bitfinder_1_index}), .Y(mux_11_bit_1_out), .X_Y(COMP_with_28_x_y[0]),
    .DIFFERENCE(COMP_with_28_difference));  // open: LARGER
  Shifter #(.width(32), .shift("lr")) shifter_1 (.in(Fraction), .\dist (COMP_with_28_difference), .out(shifter_1_out));
  Shifter #(.width(32)) shifter_2 (.in(Fraction), .\dist (COMP_with_28_difference), .out(shifter_2_out));
  ALU_16_bit alu_16_bit_1 (
    .ALU_A_IN({{5{1'b0}}, Exponent}), .ALU_B_IN({{11{1'b0}}, COMP_with_28_difference}),
    .OP_CODE({2'b00, COMP_with_28_x_y[0]}), .ALU_OUT(alu_16_bit_1_alu_out), .Z(alu_16_bit_1_z),
    .N(alu_16_bit_1_n));
  // _7408 7408_1: pin names not known; wires that end beside it: alu_16_bit_1_z, bitfinder_1_found, n7408_1_p3
  // _7432 7432_1: pin names not known; wires that end beside it: n7408_1_p3, alu_16_bit_1_n, UNDERFLOW
  MUX_32_bit MUX (._0(shifter_1_out), ._1(shifter_2_out), .S(COMP_with_28_x_y[0]), .out_4(NORMALIZED_FRACTION));
  ALU_16_bit alu_16_bit_2 (
    .ALU_A_IN(16'h7fe), .ALU_B_IN(alu_16_bit_1_alu_out), .OP_CODE(3'b001), .N(OVERFLOW));  // open: ALU_OUT, Z
  MUX_11_bit mux_11_bit_2 (
    .in_1({11{1'b0}}), ._1(alu_16_bit_1_alu_out[10:0]), .SELECT(bitfinder_1_found), .OUT(NORMALIZED_EXPONENT));

  // Notes on the sheet:
  //   find leading 1
  //   exp (16 bit)
  //   diff (16 bit)
  //   left shift if less than 28
  //   else right shift
endmodule

module Rounder (
  input  [31:0] Normalized_32_bits,
  output [31:0] ROUNDED
);

  wire n7432_1_p1, n7432_1_p3, n7432_1_p6;
  wire [0:0] n7408_1_p3;
  wire [31:24] alu_32_bit_1_c;

  // _7432 7432_1: pin names not known; wires that end beside it: n7432_1_p1, Normalized_32_bits[6], n7432_1_p3, n7432_1_p3, Normalized_32_bits[8], n7432_1_p6, 1'b0, 1'b1
  // _7408 7408_1: pin names not known; wires that end beside it: Normalized_32_bits[7], n7432_1_p6, n7408_1_p3[0], 1'b0, 1'b1
  BitFinder #(.width(6), .\type ("high1")) bitfinder_1 (
    .in(Normalized_32_bits[5:0]), .found(n7432_1_p1));  // open: index
  ALU_32_bit alu_32_bit_1 (
    .OpCode({6{1'b0}}), .Invert_B_Signal(1'b0), .A({{8{1'b0}}, Normalized_32_bits[31:8]}),
    .B({{31{1'b0}}, n7408_1_p3[0]}), .Cin(1'b0), .C({alu_32_bit_1_c, ROUNDED[31:8]}));  // open: Cout, OVF

  assign ROUNDED[7:0] = {8{1'b0}};

  // Notes on the sheet:
  //   S
  //   G
  //   R
  //   G(LSB+R+S)
endmodule

module MUX_32_bit (
  input  [31:0] _0,
  input  [31:0] _1,
  input  S,
  output [31:0] out_4
);

  // _74157 74157_1: pin names not known
  // _74157 74157_2: pin names not known; wires that end beside it: S, _0[0], _1[0], out_4[0], _0[1], _1[1], out_4[1], 1'b0, _0[2], _1[2], out_4[2], _0[3], _1[3], out_4[3]
  // _74157 74157_3: pin names not known; wires that end beside it: S, _0[4], _1[4], out_4[4], _0[5], _1[5], out_4[5], 1'b0, _0[7], _1[7], out_4[7], _0[6], _1[6], out_4[6]
  // _74157 74157_4: pin names not known; wires that end beside it: S, _0[8], _1[8], out_4[8], _0[9], _1[9], out_4[9], 1'b0, _0[11], _1[11], out_4[11], _0[10], _1[10], out_4[10]
  // _74157 74157_5: pin names not known; wires that end beside it: S, _0[12], _1[12], out_4[12], _0[13], _1[13], out_4[13], 1'b0, _0[15], _1[15], out_4[15], _0[14], _1[14], out_4[14]
  // _74157 74157_6: pin names not known; wires that end beside it: S, _0[16], _1[16], out_4[16], _0[17], _1[17], out_4[17], 1'b0, _0[19], _1[19], out_4[19], _0[18], _1[18], out_4[18]
  // _74157 74157_7: pin names not known; wires that end beside it: S, _0[20], _1[20], out_4[20], _0[21], _1[21], out_4[21], 1'b0, _0[23], _1[23], out_4[23], _0[22], _1[22], out_4[22]
  // _74157 74157_8: pin names not known; wires that end beside it: S, _0[24], _1[24], out_4[24], _0[25], _1[25], out_4[25], 1'b0, _0[27], _1[27], out_4[27], _0[26], _1[26], out_4[26]
  // _74157 74157_9: pin names not known; wires that end beside it: S, _0[28], _1[28], out_4[28], _0[29], _1[29], out_4[29], 1'b0, _0[31], _1[31], out_4[31], _0[30], _1[30], out_4[30]
endmodule

module Floating_point_adder (
  input  [31:0] X,
  input  [31:0] Y,
  output [31:0] Out,
  output OVERFLOW,
  output UNDERFLOW
);

  wire comparator_1_x_y, normalizer_1_overflow, normalizer_1_underflow, normalizer_2_overflow,
       normalizer_2_underflow;
  wire [4:0] comparator_1_difference;
  wire [7:0] normalizer_2_normalized_fraction;
  wire [10:0] comparator_1_larger, normalizer_1_normalized_exponent;
  wire [23:20] normalizer_2_normalized_fraction_2;
  wire [30:0] alu_32_bit_1_c;
  wire [31:0] fraction_sign_1_output, fraction_sign_2_output, fraction_sign_3_output, mux_32_bit_1_out_4,
       mux_32_bit_2_out_4, normalizer_1_normalized_fraction, rounder_1_rounded, shifter_1_out;

  Fraction_Sign fraction_sign_1 (
    .Sign(X[31]), .Fraction({4'b0001, X[19:0], {8{1'b0}}}), .Exponent(X[30:20]),
    .\output (fraction_sign_1_output));
  comparator comparator_1 (
    .X(X[30:20]), .Y(Y[30:20]), .X_Y(comparator_1_x_y), .LARGER(comparator_1_larger),
    .DIFFERENCE(comparator_1_difference));
  Fraction_Sign fraction_sign_2 (
    .Sign(Y[31]), .Fraction({4'b0001, Y[19:0], {8{1'b0}}}), .Exponent(Y[30:20]),
    .\output (fraction_sign_2_output));
  MUX_32_bit mux_32_bit_1 (
    ._0(fraction_sign_1_output), ._1(fraction_sign_2_output), .S(comparator_1_x_y), .out_4(mux_32_bit_1_out_4));
  Fraction_Sign fraction_sign_3 (
    .Sign(Out[31]), .Fraction({Out[31], alu_32_bit_1_c}), .Exponent(11'h1), .\output (fraction_sign_3_output));
  Normalizer normalizer_1 (
    .Fraction(fraction_sign_3_output), .Exponent(comparator_1_larger),
    .NORMALIZED_FRACTION(normalizer_1_normalized_fraction),
    .NORMALIZED_EXPONENT(normalizer_1_normalized_exponent), .OVERFLOW(normalizer_1_overflow),
    .UNDERFLOW(normalizer_1_underflow));
  MUX_32_bit mux_32_bit_2 (
    ._0(fraction_sign_2_output), ._1(fraction_sign_1_output), .S(comparator_1_x_y), .out_4(mux_32_bit_2_out_4));
  Shifter #(.width(32), .shift("lr")) shifter_1 (
    .in(mux_32_bit_2_out_4), .\dist (comparator_1_difference), .out(shifter_1_out));
  Rounder rounder_1 (.Normalized_32_bits(normalizer_1_normalized_fraction), .ROUNDED(rounder_1_rounded));
  ALU_32_bit alu_32_bit_1 (
    .OpCode({6{1'b0}}), .Invert_B_Signal(1'b0), .A(mux_32_bit_1_out_4), .B(shifter_1_out), .Cin(1'b0),
    .C({Out[31], alu_32_bit_1_c}));  // open: Cout, OVF
  Normalizer normalizer_2 (
    .Fraction(rounder_1_rounded), .Exponent(normalizer_1_normalized_exponent),
    .NORMALIZED_FRACTION({normalizer_2_normalized_fraction_2, Out[19:0], normalizer_2_normalized_fraction}),
    .NORMALIZED_EXPONENT(Out[30:20]), .OVERFLOW(normalizer_2_overflow), .UNDERFLOW(normalizer_2_underflow));
  // _7432 7432_1: pin names not known; wires that end beside it: normalizer_2_overflow, normalizer_1_overflow, OVERFLOW, normalizer_1_underflow, normalizer_2_underflow, UNDERFLOW

  // Notes on the sheet:
  //   Exponent Compare 
  //   Exponent
  //   Fraction_Sign
  //   Sign check
  //   Fraction_Sign
  //   32 bit MUX
  //   Larger
  //   32 bit MUX
  //   Normalizer
  //   Smaller
  //   Rounder
  //   Shift Smaller Number Right
  //   Op Code
  //   Normalizer
  //   32 bit ALU
endmodule
