// Logisim project Nand.circ as structural Verilog: 1 circuit, main circuit main
module main (
  input  _1__1A,
  input  _14__Vcc,
  input  _2__1B,
  input  _13__NC,
  input  _3__1C,
  input  _12__1H,
  input  _4__1D,
  input  _11__1G,
  input  _5__1E,
  input  _10__NC,
  input  _6__1F,
  input  _9__NC,
  output _8__3Y
);

  nand \nand  (_8__3Y, _6__1F, _5__1E, _4__1D, _3__1C, _2__1B, _1__1A, _12__1H, _11__1G);
endmodule
