// Logisim project temp.circ as structural Verilog: 1 circuit, main circuit main
module main (
  input  Bo,
  input  B1,
  input  Ao,
  input  A1,
  input  B2,
  input  B3,
  input  A2,
  input  A3,
  input  CS0,
  input  CS1,
  input  CS3,
  output Xo,
  output Yo,
  output X2,
  output Y2,
  output X3,
  output Y3,
  output X1,
  output Y1,
  output Zo
);

  wire n7404_1_p2, n7404_1_p4, n7404_1_p6, n7404_1_p10, n7404_1_p11, n7404_2_p6, n7404_2_p10, n7404_2_p12,
       n7404_2_p14, n7408_1_p3, n7408_1_p6, n7408_1_p11, n7408_1_p14, n7408_2_p3, n7408_3_p3, n7408_3_p4,
       n7408_3_p6, n7408_3_p11, n7408_3_p12, n7408_3_p14, n7408_4_p3, n7408_4_p6, n7408_4_p10, n7408_4_p13,
       n7408_5_p3, n7408_5_p6, n7408_5_p9, n7408_5_p12, n7408_6_p3, n7408_6_p4, n7408_6_p6, n7408_6_p11,
       n7408_6_p12, n7408_6_p14, n7432_1_p3, n7432_2_p3, n7432_3_p3, n7432_4_p3, n74138_1_p7, n74138_1_p10,
       n74138_1_p11, n74138_1_p12, n74138_1_p13, n74138_1_p14, n74138_1_p15, n74138_1_p16;

  // _74138 74138_1: pin names not known; wires that end beside it: CS0, CS1, CS3, 1'b0, 1'b0, 1'b1, n74138_1_p7, 1'b0, 1'b1, n74138_1_p10, n74138_1_p11, n74138_1_p12, n74138_1_p13, n74138_1_p14, n74138_1_p15, n74138_1_p16
  // _7408 7408_1: pin names not known; wires that end beside it: n74138_1_p11, n74138_1_p7, n7408_1_p3, n74138_1_p12, n74138_1_p16, n7408_1_p6, 1'b0, 1'b1, n74138_1_p13, n74138_1_p14, n7408_1_p11, n7408_1_p11, n74138_1_p15, n7408_1_p14
  // _7404 7404_1: pin names not known; wires that end beside it: n7408_1_p3, n7404_1_p2, n7408_1_p6, n7404_1_p4, n74138_1_p10, n7404_1_p6, 1'b0, 1'b1, n7408_1_p14, n7404_1_p10, n7404_1_p11, Zo
  // _7408 7408_2: pin names not known; wires that end beside it: n74138_1_p11, n74138_1_p14, n7408_2_p3, n7408_2_p3, n74138_1_p15, n7404_1_p11, 1'b0, 1'b1
  // _7408 7408_3: pin names not known; wires that end beside it: Ao, n7408_1_p3, n7408_3_p3, n7408_3_p4, n7404_1_p2, n7408_3_p6, 1'b0, 1'b1, n7404_1_p4, Bo, n7408_3_p11, n7408_3_p12, n7404_1_p10, n7408_3_p14
  // _7404 7404_2: pin names not known; wires that end beside it: Ao, n7408_3_p4, Bo, n7408_3_p12, A1, n7404_2_p6, 1'b0, 1'b1, B1, n7404_2_p10, A2, n7404_2_p12, B2, n7404_2_p14, 1'b0
  // _7432 7432_1: pin names not known; wires that end beside it: n7408_3_p3, n7408_3_p6, n7432_1_p3, n7432_1_p3, n7408_3_p11, Xo, 1'b1, n7404_1_p6, n7408_3_p14, Yo
  // _7408 7408_4: pin names not known; wires that end beside it: A1, n7408_1_p3, n7408_4_p3, n7404_2_p6, n7404_1_p2, n7408_4_p6, 1'b0, n7404_1_p4, B1, n7408_4_p10, n7404_2_p10, n7404_1_p10, n7408_4_p13
  // _7432 7432_2: pin names not known; wires that end beside it: n7408_4_p3, n7408_4_p6, n7432_2_p3, n7432_2_p3, n7408_4_p10, X1, 1'b0, 1'b1, n7404_1_p6, n7408_4_p13, Y1
  // _7408 7408_5: pin names not known; wires that end beside it: A2, n7408_1_p3, n7408_5_p3, n7404_2_p12, n7404_1_p2, n7408_5_p6, n7404_1_p4, B2, n7408_5_p9, n7404_2_p14, n7404_1_p10, n7408_5_p12
  // _7432 7432_3: pin names not known; wires that end beside it: n7408_5_p3, n7408_5_p6, n7432_3_p3, n7432_3_p3, n7408_5_p9, X2, 1'b1, n7404_1_p6, n7408_5_p12, Y2
  // _7408 7408_6: pin names not known; wires that end beside it: A3, n7408_1_p3, n7408_6_p3, n7408_6_p4, n7404_1_p2, n7408_6_p6, 1'b0, 1'b1, n7404_1_p4, B3, n7408_6_p11, n7408_6_p12, n7404_1_p10, n7408_6_p14
  // _7404 7404_3: pin names not known; wires that end beside it: A3, n7408_6_p4, B3, n7408_6_p12, 1'b0, 1'b0
  // _7432 7432_4: pin names not known; wires that end beside it: n7408_6_p3, n7408_6_p6, n7432_4_p3, n7432_4_p3, n7408_6_p11, X3, 1'b1, n7404_1_p6, n7408_6_p14, Y3

  // Notes on the sheet:
  //   AND
  //   NOT
  //   AND
  //   Xi er part
  //   Xi er part
  //   Xi er part
  //   Yi er part
  //   Yi er part
endmodule
